# Fritzing sketch lobstar-0.2.1 (saved by Fritzing 0.8.3b)
circuit board: 5.65695cm x 2.17967cm
breadboards: 1

parts:
  J3 = male pin header, 14 pins [form="♂ (male)"]
  J2 = male pin header, 14 pins [form="♂ (male)"]
  Y1 = Resonator [frequency="16 Mhz" package=THT]
  R1 = Resistor [tolerance=±5% resistance=10k package=THT]
  S1 = Pushbutton [package="[THT]"]
  U1 = atmega328 [package=dip]
  C1 = Ceramic Capacitor [capacitance=100nF voltage=16V package="200 mil [THT, multilayer]"]
  FTDI = ftdi [form="♂ (male)"]

nets:
  N1: J3.pin1, U1.A5
  N2: J3.pin2, U1.A4
  N3: J3.pin3, U1.A3
  N4: J3.pin4, U1.A2
  N5: J3.pin5, U1.A1
  N6: J3.pin6, U1.A0
  GND: J3.pin7, J2.pin8, Y1.GND, S1.Pin_3, S1.Pin_4, U1.GND, FTDI.connector5
  N7: J3.pin8, U1.AREF
  N8: J3.pin9, J2.pin7, R1.Pin_0, U1.VCC, U1.AVCC, FTDI.connector3
  N9: J3.pin10, U1.D13
  N10: J3.pin11, U1.D12
  N11: J3.pin12, U1.D11_(PWM)
  N12: J3.pin13, U1.D10_(PWM)
  N13: J3.pin14, U1.D9_(PWM)
  N14: J2.pin1, R1.Pin_1, S1.Pin_1, S1.Pin_2, U1.RESET, C1.1
  N15: J2.pin2, U1.D0_(RX), FTDI.connector2
  N16: J2.pin3, U1.D1_(TX), FTDI.connector1
  N17: J2.pin4, U1.D2
  N18: J2.pin5, U1.D3_(PWM)
  N19: J2.pin6, U1.D4
  N20: J2.pin9, Y1.0, U1.XLAT1
  N21: J2.pin10, Y1.pin_1, U1.XLAT2
  N22: J2.pin11, U1.D5_(PWM)
  N23: J2.pin12, U1.D6_(PWM)
  N24: J2.pin13, U1.D7
  N25: J2.pin14, U1.D8
  N26: C1.0, FTDI.connector0

notes:
  lobstar 0.2.1
  grn
  blk
