# Fritzing sketch lobstar-0.2 (saved by Fritzing 0.8.3b)
circuit board: 7.44911cm x 2.85277cm
breadboards: 1

parts:
  J3 = male pin header, 14 pins [form="♂ (male)"]
  J2 = male pin header, 14 pins [form="♂ (male)"]
  C1 = Ceramic Capacitor [capacitance=0.1nF package="100 mil [THT, multilayer]"]
  Y1 = Resonator [frequency="16 Mhz" package=THT]
  R1 = Resistor [tolerance=±5% resistance=1k package=THT]
  U1 = atmega168 [package=dip]
  J4 = FTDI Conector [form="♂ (male)" package=THT]

nets:
  N1: J3.pin1, U1.A5
  N2: J3.pin2, U1.A4
  N3: J3.pin3, U1.A3
  N4: J3.pin4, U1.A2
  N5: J3.pin5, U1.A1
  N6: J3.pin6, U1.A0
  GND: J3.pin7, J2.pin8, Y1.GND, U1.GND, J4.GND
  N7: J3.pin8, U1.AREF
  VCC: J3.pin9, J2.pin7, R1.Pin_0, U1.VCC, U1.AVCC, J4.Vcc
  N8: J3.pin10, U1.D13
  N9: J3.pin11, U1.D12
  N10: J3.pin12, U1.D11_(PWM)
  N11: J3.pin13, U1.D10_(PWM)
  N12: J3.pin14, U1.D9_(PWM)
  N13: J2.pin1, C1.1, R1.Pin_1, U1.RESET
  N14: J2.pin2, U1.D0_(RX), J4.TXD
  N15: J2.pin3, U1.D1_(TX), J4.RXD
  N16: J2.pin4, U1.D2
  N17: J2.pin5, U1.D3_(PWM)
  N18: J2.pin6, U1.D4
  N19: J2.pin9, Y1.0, U1.XLAT1
  N20: J2.pin10, Y1.pin_1, U1.XLAT2
  N21: J2.pin11, U1.D5_(PWM)
  N22: J2.pin12, U1.D6_(PWM)
  N23: J2.pin13, U1.D7
  N24: J2.pin14, U1.D8
  N25: C1.0, J4.RTS#

notes:
  lobstar 0.2

custom parts:
  FTDI Conector: Generic male header
