# Fritzing sketch lobstar-filled (saved by Fritzing 0.8.3b)
circuit board: 5.93217cm x 2.52822cm
breadboards: 1

parts:
  U1 = atmega168 [package=dip]
  J1 = male pin header, 6 pins [form="♂ (male)"]
  J3 = male pin header, 14 pins [form="♂ (male)"]
  J2 = male pin header, 14 pins [form="♂ (male)"]
  C1 = Ceramic Capacitor [capacitance=0.1nF package="100 mil [THT, multilayer]"]
  Y1 = Resonator [frequency="16 Mhz" package=THT]
  R1 = Resistor [tolerance=±5% resistance=1k package=THT]

nets:
  N1: U1.RESET, J2.pin1, C1.1, R1.Pin_1
  N2: U1.D0_(RX), J1.pin3, J2.pin2
  N3: U1.D1_(TX), J1.pin2, J2.pin3
  N4: U1.D2, J2.pin4
  N5: U1.D3_(PWM), J2.pin5
  N6: U1.D4, J2.pin6
  N7: U1.VCC, U1.AVCC, J1.pin6, J3.pin9, J2.pin7, R1.Pin_0
  GND: U1.GND, J1.pin4, J3.pin7, J2.pin8, Y1.GND
  N8: U1.XLAT1, J2.pin9, Y1.0
  N9: U1.XLAT2, J2.pin10, Y1.pin_1
  N10: U1.D5_(PWM), J2.pin11
  N11: U1.D6_(PWM), J2.pin12
  N12: U1.D7, J2.pin13
  N13: U1.D8, J2.pin14
  N14: U1.D9_(PWM), J3.pin14
  N15: U1.D10_(PWM), J3.pin13
  N16: U1.D11_(PWM), J3.pin12
  N17: U1.D12, J3.pin11
  N18: U1.D13, J3.pin10
  N19: U1.AREF, J3.pin8
  N20: U1.A0, J3.pin6
  N21: U1.A1, J3.pin5
  N22: U1.A2, J3.pin4
  N23: U1.A3, J3.pin3
  N24: U1.A4, J3.pin2
  N25: U1.A5, J3.pin1
  N26: J1.pin1, C1.0

notes:
  boarduinette v 0.1
